# Fritzing sketch wiring (saved by Fritzing 0.9.2b)
breadboards: 1

parts:
  "Forward"_button = Pushbutton [package="[THT]"]
  "Back"_Button = Pushbutton [package="[THT]"]
  R1 = Resistor [tolerance=±5% resistance=1k package=THT]
  R2 = Resistor [tolerance=±5% resistance=1k package=THT]
  R3 = Resistor [tolerance=±5% resistance=1k package=THT]
  LED1 = LED - 5mm [color="Red (633nm)" package="5 mm [THT]"]
  Raspberry_Pi1 = Raspberry Pi 2

nets:
  N1: "Forward"_button.Pin_1, "Forward"_button.Pin_2
  N2: "Forward"_button.Pin_3, "Forward"_button.Pin_4, R1.Pin_1
  N3: "Back"_Button.Pin_1, "Back"_Button.Pin_2, Raspberry_Pi1.3v3, Raspberry_Pi1.GPIO2
  N4: "Back"_Button.Pin_3, "Back"_Button.Pin_4, R2.Pin_1
  N5: R1.Pin_0, Raspberry_Pi1.GPIO27, Raspberry_Pi1.GPIO22
  N6: R2.Pin_0, R3.Pin_0, Raspberry_Pi1.GND, Raspberry_Pi1.GPIO18, Raspberry_Pi1.GPIO14
  N7: R3.Pin_1, LED1.cathode
  N8: LED1.anode, Raspberry_Pi1.GPIO17
